// Logisim project test.circ as structural Verilog: 2 circuits, main circuit main
module main (
  input  in_1
);

  wire outnet;

  // Probe on in_1
  // Probe on outnet
  not not_1 (outnet, in_1);
  // Probe on outnet

  // Other names for the same wires on the sheet: innet = in_1
endmodule

module inner_circuit (
  input  plus_1,
  input  plus_10,
  input  reset,
  input  clk,
  output [7:0] res
);

  wire [7:0] adder_1_out, adder_2_out, multiplexer_1_out, multiplexer_2_out, multiplexer_3_out;

  Adder adder_1 (.a(res), .b(8'h1), .out(adder_1_out));  // open: cin, cout
  Adder adder_2 (.a(res), .b(8'ha), .out(adder_2_out));  // open: cin, cout
  Multiplexer #(.width(8), .enable("false")) multiplexer_1 (
    .in0(res), .in1(adder_1_out), .out(multiplexer_1_out), .sel(plus_1));
  Multiplexer #(.width(8), .enable("false")) multiplexer_2 (
    .in0(multiplexer_1_out), .in1(adder_2_out), .out(multiplexer_2_out), .sel(plus_10));
  Multiplexer #(.width(8), .enable("false")) multiplexer_3 (
    .in0(multiplexer_2_out), .in1({8{1'b0}}), .out(multiplexer_3_out), .sel(reset));
  Register register_1 (.D(multiplexer_3_out), .en(1'b1), .Q(res), .clk(clk));  // open: clr

  // Other names for the same wires on the sheet: reg_out[7:0] = res
endmodule
